# Fritzing sketch 6NOT (saved by Fritzing 1.0.5)
breadboards: 1

parts:
  VCC1 = Battery [internal_resistance=0.1Ω]
  U1 = 74HC04_HEX_INVERTER [package=dil14]
  LED1 = LED - 5mm [color="Red (633nm)" current=0.030A package="5 mm [THT]"]

nets:
  N1: VCC1.-, U1.GND, LED1.cathode
  N2: VCC1.+, U1.1A, U1.VCC
  N3: U1.1Y, U1.2A
  N4: U1.2Y, U1.3A
  N5: U1.3Y, U1.4A
  N6: U1.4Y, U1.5A
  N7: U1.5Y, U1.6A
  N8: U1.6Y, LED1.anode
