# Fritzing sketch Basic LED (saved by Fritzing 1.0.5)
breadboards: 1

parts:
  VCC1 = Battery [internal_resistance=0.1Ω]
  LED1 = LED - 3mm [color="Red (633nm)" current=30mA package="3 mm [THT]"]
  R1 = Resistor [tolerance=±5% resistance=220 package="1206 [SMD]"]

nets:
  N1: VCC1.-, LED1.cathode
  N2: VCC1.+, R1.Pin_0
  N3: LED1.anode, R1.Pin_1
