// Logisim project 4Bit_Adder_Subtracker.circ as structural Verilog: 1 circuit, main circuit main
module main (
  input  Cin,
  input  b0,
  input  a0,
  input  b1,
  input  a1,
  input  b2,
  input  a2,
  input  b3,
  input  a3,
  output s0,
  output s1,
  output s2,
  output s3,
  output Cout
);

  wire and_1_out, and_2_out, and_3_out, and_4_out, and_5_out, and_6_out, and_7_out, and_8_out, or_1_out,
       or_2_out, or_3_out, xor_1_out, xor_2_out, xor_3_out, xor_4_out, xor_5_out, xor_6_out, xor_7_out,
       xor_8_out;

  xor xor_1 (xor_1_out, Cin, b0);
  xor xor_2 (xor_2_out, Cin, b1);
  xor xor_3 (xor_3_out, Cin, b2);
  xor xor_4 (xor_4_out, Cin, b3);
  xor xor_5 (xor_5_out, xor_1_out, a0);
  and and_1 (and_1_out, xor_1_out, a0);
  xor xor_6 (xor_6_out, xor_2_out, a1);
  and and_2 (and_2_out, xor_2_out, a1);
  and and_3 (and_3_out, xor_3_out, a2);
  and and_4 (and_4_out, xor_4_out, a3);
  xor xor_7 (xor_7_out, xor_3_out, a2);
  xor xor_8 (xor_8_out, xor_4_out, a3);
  and and_5 (and_5_out, xor_5_out, Cin);
  and and_6 (and_6_out, xor_6_out, or_1_out);
  and and_7 (and_7_out, xor_7_out, or_2_out);
  and and_8 (and_8_out, xor_8_out, or_3_out);
  xor xor_9 (s0, xor_5_out, Cin);
  xor xor_10 (s1, xor_6_out, or_1_out);
  xor xor_11 (s2, xor_7_out, or_2_out);
  xor xor_12 (s3, xor_8_out, or_3_out);
  or or_1 (or_1_out, and_5_out, and_1_out);
  or or_2 (or_2_out, and_6_out, and_2_out);
  or or_3 (or_3_out, and_7_out, and_3_out);
  or or_4 (Cout, and_8_out, and_4_out);
endmodule
