// Logisim project Experiment2.1.1.circ as structural Verilog: 1 circuit, main circuit main
module main (
  input  D,
  input  C,
  input  B,
  input  A,
  input  S_in,
  input  Mode,
  output Q_D,
  output Q_C,
  output Q_B,
  output Q_A
);

  wire and_1_out, and_2_out, and_3_out, and_4_out, and_5_out, and_6_out, and_7_out, and_8_out, Clock_out,
       not_1_out, or_1_out, or_2_out, or_3_out, or_4_out;

  Button Clock (.out(Clock_out));
  D_Flip_Flop d_ff_1 (.D(or_1_out), .clk(Clock_out), .Q(Q_D));  // open: Qn, preset, reset
  D_Flip_Flop d_ff_2 (.D(or_2_out), .clk(Clock_out), .Q(Q_C));  // open: Qn, preset, reset
  D_Flip_Flop d_ff_3 (.D(or_3_out), .clk(Clock_out), .Q(Q_B));  // open: Qn, preset, reset
  D_Flip_Flop d_ff_4 (.D(or_4_out), .clk(Clock_out), .Q(Q_A));  // open: Qn, preset, reset
  or or_1 (or_1_out, and_1_out, and_2_out);
  or or_2 (or_2_out, and_3_out, and_4_out);
  or or_3 (or_3_out, and_5_out, and_6_out);
  or or_4 (or_4_out, and_7_out, and_8_out);
  and and_1 (and_1_out, D, Mode);
  and and_2 (and_2_out, not_1_out, Q_C);
  and and_3 (and_3_out, C, Mode);
  and and_4 (and_4_out, not_1_out, Q_B);
  and and_5 (and_5_out, B, Mode);
  and and_6 (and_6_out, not_1_out, Q_A);
  and and_7 (and_7_out, A, Mode);
  and and_8 (and_8_out, not_1_out, S_in);
  not not_1 (not_1_out, Mode);
endmodule
